# Fritzing sketch circuit (saved by Fritzing 0.9.3b)
breadboards: 1

parts:
  Componente1 = Arduino Uno (Rev3)
  S1 = Pushbutton [package="[SMD]"]
  R1 = Resistor [tolerance=±5% resistance=3.3k package="0603 [SMD]"]
  LCM1602_IIC2 = LCM1602 IIC [part_number="LCM1602 IIC" chip_label="LCM1602 IIC" package="DIP (Dual Inline) [THT]"]
  U2 = LCD-16X2 [package=lcd-16x2_noholes]

nets:
  N1: Componente1.A4/SDA, LCM1602_IIC2.SDA
  N2: Componente1.A5/SCL, LCM1602_IIC2.SCL
  N3: Componente1.D11_PWM/MOSI, S1.Pin_1, S1.Pin_2, R1.Pin_1
  5V: Componente1.5V, S1.Pin_3, S1.Pin_4, LCM1602_IIC2.VCC
  GND: Componente1.GND, R1.Pin_0, LCM1602_IIC2.GND
  VSS: LCM1602_IIC2.VSS, U2.VSS
  VDD: LCM1602_IIC2.VDD, U2.VDD
  N4: LCM1602_IIC2.V0, U2.VO
  N5: LCM1602_IIC2.RS, U2.RS
  N6: LCM1602_IIC2.RW, U2.R_W
  N7: LCM1602_IIC2.E, U2.E
  N8: LCM1602_IIC2.D0, U2.DB0
  N9: LCM1602_IIC2.D1, U2.DB1
  N10: LCM1602_IIC2.D2, U2.DB2
  N11: LCM1602_IIC2.D3, U2.DB3
  N12: LCM1602_IIC2.D4, U2.DB4
  N13: LCM1602_IIC2.D5, U2.DB5
  N14: LCM1602_IIC2.D6, U2.DB6
  N15: LCM1602_IIC2.D7, U2.DB7
  N16: LCM1602_IIC2.A, U2.A
  N17: LCM1602_IIC2.K, U2.K

custom parts:
  LCM1602 IIC: I2C-Module to use a 1602 or 2004 LCD on with the wire.h libory Serial LCD Modul
